# Fritzing sketch Sketch (saved by Fritzing 0.9.9b)
breadboards: 1

parts:
  MH-ET_LIVE_ESP32_DEVKIT1 = MH-ET LIVE ESP32 DEVKIT 38 pins
  GND_bridge = Raspberry Pi 4B
  Vcc_5V = Infrared Proximity Sensor

nets:
  GND: MH-ET_LIVE_ESP32_DEVKIT1.GND, GND_bridge.GND, Vcc_5V.GND
  N1: MH-ET_LIVE_ESP32_DEVKIT1.TXD0, Vcc_5V.Vout
  5V: GND_bridge.5V, Vcc_5V.Vcc

notes:
  Vout 3.3V

custom parts:
  MH-ET LIVE ESP32 DEVKIT 38 pins: http://mh.nodebb.com/topic/2/mh-et-live-esp32-devkit
